# Fritzing sketch Diag (saved by Fritzing 0.9.3b)
breadboards: 1

parts:
  Part2 = Arduino Uno (Rev3)
  U1 = ESP8266 WiFi Module [part_number=ESP8266]
  RHT1 = Humidity and Temperature Sensor RHT03
  J1 = Piezo Speaker
  LED1 = LED - 5mm [color="Red (633nm)" package="5 mm [THT]"]

nets:
  GND: Part2.GND, U1.GND, U1.GPIO_15, RHT1.GND_1, J1.pin1, LED1.cathode
  N1: Part2.D2, U1.TXD
  N2: Part2.D3_PWM, U1.RXD
  N3: Part2.D7, RHT1.Data-signal
  3V3: Part2.3V3, U1.VCC, U1.CH_PD
  5V: Part2.5V, RHT1.Vcc

notes:
  PIR sensor module
